# Fritzing sketch 连线图 (saved by Fritzing 0.9.3b)
breadboards: 1

parts:
  元件1 = Arduino Nano (Rev3.0)
  S1 = Momentary Switch [package=ksa_sealed_tac_switch]
  S2 = Momentary Switch [package=ksa_sealed_tac_switch]
  S3 = Momentary Switch [package=ksa_sealed_tac_switch]
  o1 = Module display OLED I2C 128x64 SSD1306 [package=THT]
  J1 = Piezo Speaker

nets:
  GND: 元件1.GND, S1.3, S1.4, S2.3, S2.4, S3.1, S3.2, o1.GND, J1.pin1
  N1: 元件1.D3, S1.1, S1.2
  N2: 元件1.D9, J1.pin2
  N3: 元件1.D11/MOSI, S3.3, S3.4
  N4: 元件1.D12/MISO, S2.1, S2.2
  5V: 元件1.5V, o1.VCC
  N5: 元件1.A5, o1.SCL
  N6: 元件1.A4, o1.SDA

custom parts:
  Module display OLED I2C 128x64 SSD1306: Ecran OLED I2C SSD163 de 128x64 avec connexion I2C
